// Logisim project 7segment_display.circ as structural Verilog: 2 circuits, main circuit main
module main (
  input  [2:0] in_1
);

  wire n7_segment_display_decoder_pla_1_out_4, n7_segment_display_decoder_pla_1_out_5,
       n7_segment_display_decoder_pla_1_out_6, n7_segment_display_decoder_pla_1_out_7,
       n7_segment_display_decoder_pla_1_out_8, n7_segment_display_decoder_pla_1_out_9,
       n7_segment_display_decoder_pla_1_out_10;

  _7_Segment_Display u_7_segment_display_1 (
    .g(n7_segment_display_decoder_pla_1_out_4), .f(n7_segment_display_decoder_pla_1_out_5),
    .a(n7_segment_display_decoder_pla_1_out_6), .b(n7_segment_display_decoder_pla_1_out_7),
    .e(n7_segment_display_decoder_pla_1_out_8), .d(n7_segment_display_decoder_pla_1_out_9),
    .c(n7_segment_display_decoder_pla_1_out_10));  // open: dp
  _7_Segment_Display_Decoder__PLA u_7_segment_display_decoder_pla_1 (
    .A(in_1[2]), .B(in_1[1]), .C(in_1[0]), .out_4(n7_segment_display_decoder_pla_1_out_4),
    .out_5(n7_segment_display_decoder_pla_1_out_5), .out_6(n7_segment_display_decoder_pla_1_out_6),
    .out_7(n7_segment_display_decoder_pla_1_out_7), .out_8(n7_segment_display_decoder_pla_1_out_8),
    .out_9(n7_segment_display_decoder_pla_1_out_9), .out_10(n7_segment_display_decoder_pla_1_out_10));
endmodule

module _7_Segment_Display_Decoder__PLA (
  input  A,
  input  B,
  input  C,
  output out_4,
  output out_5,
  output out_6,
  output out_7,
  output out_8,
  output out_9,
  output out_10
);

  wire A_nB_out, A_nBC_out, A_nC_out, AC_out, B_nC_out, BC_out, nA_nC_out, nAB_out, nB_nC_out, not_1_out,
       not_2_out, not_3_out;

  not not_1 (not_1_out, A);
  not not_2 (not_2_out, B);
  not not_3 (not_3_out, C);
  and A_nB (A_nB_out, A, not_2_out);
  and A_nC (A_nC_out, A, not_3_out);
  and nAB (nAB_out, not_1_out, B);
  and nB_nC (nB_nC_out, not_2_out, not_3_out);
  and nA_nC (nA_nC_out, not_1_out, not_3_out);
  and AC (AC_out, A, C);
  and BC (BC_out, B, C);
  and B_nC (B_nC_out, B, not_3_out);
  and A_nBC (A_nBC_out, A, not_2_out, C);
  or O1 (out_4, A_nB_out, B_nC_out, nAB_out);
  or O2 (out_5, nB_nC_out, A_nB_out, A_nC_out);
  or O3 (out_6, nA_nC_out, AC_out, B);
  or O4 (out_7, not_1_out, nB_nC_out, BC_out);
  or O5 (out_8, B_nC_out, nA_nC_out);
  or O6 (out_9, nA_nC_out, A_nBC_out, nAB_out, B_nC_out);
  or O7 (out_10, not_2_out, C, A);

  // Notes on the sheet:
  //   (A~B)+(B~C)+(~AB)
  //   (~B~C)+(A~B)+(A~C)
  //   (~A~C)+(AC)+(B)
  //   (~A)+(~B~C)+(BC)
  //   (B~C)+(~A~C)
  //   (~A~C)+(A~BC)+(~AB)+(B~C)
  //   (~B)+(C)+(A)
endmodule
