// Logisim project nand_gates.circ as structural Verilog: 5 circuits, main circuit main
module main (
);

  OR_Gate or_1 ();  // open: in_1, in_2, out_3
  AND_Gate and_1 ();  // open: in_1, in_2, out_3
  NOT_Gate not_1 ();  // open: in_1, out_2
endmodule

module NAND_Gate (
  input  A,
  input  B,
  output X
);

  or or_1 (X, ~A, ~B);  // OR_Gate_part
endmodule

module OR_Gate (
  input  in_1,
  input  in_2,
  output out_3
);

  wire nand_1_x, nand_2_x;

  NAND_Gate nand_1 (.A(in_1), .B(in_1), .X(nand_1_x));
  NAND_Gate nand_2 (.A(in_2), .B(in_2), .X(nand_2_x));
  NAND_Gate nand_3 (.A(nand_1_x), .B(nand_2_x), .X(out_3));
endmodule

module AND_Gate (
  input  in_1,
  input  in_2,
  output out_3
);

  wire nand_1_x;

  NAND_Gate nand_1 (.A(in_1), .B(in_2), .X(nand_1_x));
  NAND_Gate nand_2 (.A(nand_1_x), .B(nand_1_x), .X(out_3));
endmodule

module NOT_Gate (
  input  in_1,
  output out_2
);

  NAND_Gate nand_1 (.A(in_1), .B(in_1), .X(out_2));
endmodule
