// Logisim project truthtable_to_circuit.circ as structural Verilog: 2 circuits, main circuit main
module main (
);

  circuit circuit_1 ();  // open: A, B, C, X, Y
endmodule

module circuit (
  input  A,
  input  B,
  input  C,
  output X,
  output Y
);

  wire nA_nB_out, nB_nC_out;

  and nA_nB (nA_nB_out, ~A, ~B);  // AND_Gate
  and nB_nC (nB_nC_out, ~B, ~C);  // AND_Gate
  or nA_nB_nB_nC (X, nB_nC_out, nA_nB_out);
  or nC_nA_nB (Y, ~C, nA_nB_out);  // OR_Gate
endmodule
