// Logisim project adder.circ as structural Verilog: 2 circuits, main circuit main
module main (
  input  A,
  input  B,
  input  Carry_In,
  output Sum,
  output Carry_Out
);

  Adder__1b adder_1b_1 (.A(A), .B(B), .Carry_In(Carry_In), .Sum(Sum), .Carry_Out(Carry_Out));
endmodule

module Adder__1b (
  input  A,
  input  B,
  input  Carry_In,
  output Sum,
  output Carry_Out
);

  wire AB_out, ACin_out, BCin_out, not_1_out, not_2_out, not_3_out;

  not not_1 (not_1_out, A);
  not not_2 (not_2_out, B);
  not not_3 (not_3_out, Carry_In);
  xor A_B_Cin (Sum, A, B, Carry_In);
  and BCin (BCin_out, B, Carry_In);
  and ACin (ACin_out, A, Carry_In);
  and AB (AB_out, A, B);
  or BCin_ACin_AB (Carry_Out, BCin_out, ACin_out, AB_out);
endmodule
