// Logisim project comparison.circ as structural Verilog: 1 circuit, main circuit main
module main (
  input  [15:0] A,
  input  [15:0] B,
  input  Carry_In,
  output [15:0] X,
  output Carry_Out,
  output Overflow,
  output [15:0] X_2,
  output Overflow_2
);

  LCU_Adder__16b lcu_adder_16b_1 (.Overflow(Overflow_2), .B(B), .A(A), .in_3(Carry_In), .Sum(X_2));  // open: PG, GG
  Adder__16b adder_16b_1 (.A(A), .B(B), .Carry_In(Carry_In), .out_4(X), .Carry_Out(Carry_Out), .Overflow(Overflow));

  // Notes on the sheet:
  //   Ripple Carry
  //   Carry Lookahead
endmodule
