// Logisim project ripple_carry_adder.circ as structural Verilog: 8 circuits, main circuit main
module main (
  input  [15:0] A,
  input  [15:0] B,
  input  Carry_In,
  output [15:0] X,
  output Carry_Out,
  output Overflow
);

  Adder__16b adder_16b_1 (.A(A), .B(B), .Carry_In(Carry_In), .out_4(X), .Carry_Out(Carry_Out), .Overflow(Overflow));
endmodule

module Adder_PLA (
  input  A,
  input  B,
  input  Carry_In,
  output Sum,
  output Carry_Out
);

  wire AB_out, ACin_out, BCin_out, not_1_out, not_2_out, not_3_out;

  not not_1 (not_1_out, A);
  not not_2 (not_2_out, B);
  not not_3 (not_3_out, Carry_In);
  xor A_B_Cin (Sum, A, B, Carry_In);
  and BCin (BCin_out, B, Carry_In);
  and ACin (ACin_out, A, Carry_In);
  and AB (AB_out, A, B);
  or BCin_ACin_AB (Carry_Out, BCin_out, ACin_out, AB_out);
endmodule

// Adder
module Adder__4b___No_Overflow_Detector (
  input  [3:0] A,
  input  [3:0] B,
  input  Carry_In,
  output [3:0] out_4,
  output Carry_Out
);

  wire adder_1b_non_msb_1_carry_out, adder_1b_non_msb_2_carry_out, adder_1b_non_msb_3_carry_out;

  Adder__1b___Non_MSB adder_1b_non_msb_1 (
    .A(A[0]), .B(B[0]), .Carry_In(Carry_In), .Sum(out_4[0]), .Carry_Out(adder_1b_non_msb_1_carry_out));
  Adder__1b___Non_MSB adder_1b_non_msb_2 (
    .A(A[1]), .B(B[1]), .Carry_In(adder_1b_non_msb_1_carry_out), .Sum(out_4[1]),
    .Carry_Out(adder_1b_non_msb_2_carry_out));
  Adder__1b___Non_MSB adder_1b_non_msb_3 (
    .A(A[2]), .B(B[2]), .Carry_In(adder_1b_non_msb_2_carry_out), .Sum(out_4[2]),
    .Carry_Out(adder_1b_non_msb_3_carry_out));
  Adder__1b___Non_MSB adder_1b_non_msb_4 (
    .A(A[3]), .B(B[3]), .Carry_In(adder_1b_non_msb_3_carry_out), .Sum(out_4[3]), .Carry_Out(Carry_Out));
endmodule

// Ripple Adder
module Adder__16b (
  input  [15:0] A,
  input  [15:0] B,
  input  Carry_In,
  output [15:0] out_4,
  output Carry_Out,
  output Overflow
);

  wire adder_4b_no_overflow_detector_1_carry_out, adder_4b_no_overflow_detector_2_carry_out,
       adder_4b_no_overflow_detector_3_carry_out;

  Adder__4b___No_Overflow_Detector adder_4b_no_overflow_detector_1 (
    .A(A[3:0]), .B(B[3:0]), .Carry_In(Carry_In), .out_4(out_4[3:0]),
    .Carry_Out(adder_4b_no_overflow_detector_1_carry_out));
  Adder__4b___No_Overflow_Detector adder_4b_no_overflow_detector_2 (
    .A(A[7:4]), .B(B[7:4]), .Carry_In(adder_4b_no_overflow_detector_1_carry_out), .out_4(out_4[7:4]),
    .Carry_Out(adder_4b_no_overflow_detector_2_carry_out));
  Adder__4b___No_Overflow_Detector adder_4b_no_overflow_detector_3 (
    .A(A[11:8]), .B(B[11:8]), .Carry_In(adder_4b_no_overflow_detector_2_carry_out), .out_4(out_4[11:8]),
    .Carry_Out(adder_4b_no_overflow_detector_3_carry_out));
  Adder__4b___With_Overflow_Detector adder_4b_with_overflow_detector_1 (
    .A(A[15:12]), .B(B[15:12]), .Carry_In(adder_4b_no_overflow_detector_3_carry_out), .out_4(out_4[15:12]),
    .Carry_Out(Carry_Out), .Overflow(Overflow));
endmodule

// Adder
module Adder__1b___Non_MSB (
  input  A,
  input  B,
  input  Carry_In,
  output Sum,
  output Carry_Out
);

  Adder_PLA adder_pla_1 (.A(A), .B(B), .Carry_In(Carry_In), .Sum(Sum), .Carry_Out(Carry_Out));
endmodule

module Overflow_Detector_PLA (
  input  A,
  input  B,
  input  Sum,
  output Overflow
);

  wire AB_nSum_out, nA_nBSum_out, not_1_out, not_2_out, not_3_out;

  not not_1 (not_1_out, A);
  not not_2 (not_2_out, B);
  not not_3 (not_3_out, Sum);
  and nA_nBSum (nA_nBSum_out, not_1_out, not_2_out, Sum);
  and AB_nSum (AB_nSum_out, A, B, not_3_out);
  or nA_nBSum_AB_nSum (Overflow, AB_nSum_out, nA_nBSum_out);
endmodule

// Adder (MSB)
module Adder__1b___MSB (
  input  A,
  input  B,
  input  Carry_In,
  output Sum,
  output Carry_Out,
  output Overflow
);

  Adder_PLA adder_pla_1 (.A(A), .B(B), .Carry_In(Carry_In), .Sum(Sum), .Carry_Out(Carry_Out));
  Overflow_Detector_PLA overflow_detector_pla_1 (.A(A), .B(B), .Sum(Sum), .Overflow(Overflow));
endmodule

// Adder MSB)
module Adder__4b___With_Overflow_Detector (
  input  [3:0] A,
  input  [3:0] B,
  input  Carry_In,
  output [3:0] out_4,
  output Carry_Out,
  output Overflow
);

  wire adder_1b_non_msb_1_carry_out, adder_1b_non_msb_2_carry_out, adder_1b_non_msb_3_carry_out;

  Adder__1b___Non_MSB adder_1b_non_msb_1 (
    .A(A[0]), .B(B[0]), .Carry_In(Carry_In), .Sum(out_4[0]), .Carry_Out(adder_1b_non_msb_1_carry_out));
  Adder__1b___Non_MSB adder_1b_non_msb_2 (
    .A(A[1]), .B(B[1]), .Carry_In(adder_1b_non_msb_1_carry_out), .Sum(out_4[1]),
    .Carry_Out(adder_1b_non_msb_2_carry_out));
  Adder__1b___Non_MSB adder_1b_non_msb_3 (
    .A(A[2]), .B(B[2]), .Carry_In(adder_1b_non_msb_2_carry_out), .Sum(out_4[2]),
    .Carry_Out(adder_1b_non_msb_3_carry_out));
  Adder__1b___MSB adder_1b_msb_1 (
    .A(A[3]), .B(B[3]), .Carry_In(adder_1b_non_msb_3_carry_out), .Sum(out_4[3]), .Carry_Out(Carry_Out),
    .Overflow(Overflow));
endmodule
