// Logisim project counter_patryk.circ as structural Verilog: 1 circuit, main circuit Counter (16b)
// Counter
module Counter__16b (
  input  C,
  input  [15:0] D,
  output [15:0] O
);

  wire comparator_1_eq, comparator_1_gt, comparator_1_lt, or_1_out;
  wire [15:0] lcu_adder_16b_1_sum;

  Comparator #(.width(16), .mode("unsigned")) comparator_1 (
    .a(O), .b(D), .gt(comparator_1_gt), .eq(comparator_1_eq), .lt(comparator_1_lt));
  Register__16b register_16b_1 (.reset(or_1_out), .write(comparator_1_lt), .C(C), .D(lcu_adder_16b_1_sum), .Q(O));
  or or_1 (or_1_out, comparator_1_gt, comparator_1_eq);
  LCU_Adder__16b lcu_adder_16b_1 (.B(O), .A(16'h1), .in_3(1'b0), .Sum(lcu_adder_16b_1_sum));  // open: Overflow, PG, GG
endmodule
