// Logisim project stack_patryk.circ as structural Verilog: 2 circuits, main circuit Stack (16b)
// Stack
module Stack__16b (
  input  Push,
  input  Pop,
  input  Reset,
  input  [15:0] Data,
  output [15:0] Top_of_Stack,
  output Error
);

  wire and_1_out, and_2_out, C_out, OpSync_q, or_1_out, Push_Pop_q, Subtraction_overflow, xor_1_out;
  wire [15:0] Addition_sum, multiplexer_1_out, multiplexer_2_out, multiplexer_3_out, ram_1_data,
       Stack_Pointer_q, Subtraction_sum;

  and and_1 (and_1_out, ~Push, ~Pop);  // AND_Gate
  xor xor_1 (xor_1_out, Push, Pop);
  and and_2 (and_2_out, xor_1_out, ~Error);  // AND_Gate
  D_Flip_Flop Push_Pop (.clk(C_out), .D(Pop), .Q(Push_Pop_q));  // open: Qn, preset, en, reset
  LCU_Adder__16b Subtraction (
    .Overflow(Subtraction_overflow), .B({16{1'b1}}), .A(Stack_Pointer_q), .in_3(1'b0), .Sum(Subtraction_sum));  // open: PG, GG
  LCU_Adder__16b Addition (.B(16'h1), .A(Stack_Pointer_q), .in_3(1'b0), .Sum(Addition_sum));  // open: Overflow, PG, GG
  D_Flip_Flop OpSync (.clk(C_out), .D(and_2_out), .Q(OpSync_q), .reset(Reset));  // open: Qn, preset, en
  Multiplexer #(.width(16), .enable("false")) multiplexer_1 (
    .in0(Data), .in1({16{1'b0}}), .out(multiplexer_1_out), .sel(Pop));
  Multiplexer #(.width(16)) multiplexer_2 (
    .in0(Addition_sum), .in1(Subtraction_sum), .out(multiplexer_2_out), .sel(Push_Pop_q), .en(OpSync_q));
  Register__16b Stack_Pointer (.reset(Reset), .write(OpSync_q), .C(C_out), .D(multiplexer_2_out), .Q(Stack_Pointer_q));
  or or_1 (or_1_out, and_1_out, Pop);
  Multiplexer #(.width(16), .enable("false")) multiplexer_3 (
    .in0(Stack_Pointer_q), .in1(Subtraction_sum), .out(multiplexer_3_out), .sel(or_1_out));
  Clock C (.out(C_out));
  RAM #(.addrWidth(16), .dataWidth(16), .bus("separate")) ram_1 (
    .addr(multiplexer_3_out), .din(multiplexer_1_out), .data(ram_1_data), .str(and_2_out), .sel(1'b1),
    .clk(C_out), .ld(1'b1), .clr(Reset));
  Exception_Detector exception_detector_1 (
    .Stack_Pointer(Stack_Pointer_q), .Push(Push), .Pop(Pop), .Sub_Overflow(Subtraction_overflow),
    .Error(Error));
  Multiplexer #(.width(16), .enable("false")) multiplexer_4 (
    .in0(ram_1_data), .in1({16{1'b0}}), .out(Top_of_Stack), .sel(and_2_out));
endmodule

module Exception_Detector (
  input  [15:0] Stack_Pointer,
  input  Push,
  input  Pop,
  input  Sub_Overflow,
  output Error
);

  wire and_1_out, and_2_out;

  and and_1 (and_1_out, Pop, Push);
  and and_2 (and_2_out, ~Stack_Pointer[15], ~Stack_Pointer[14], ~Stack_Pointer[13], ~Stack_Pointer[12], ~Stack_Pointer[11], ~Stack_Pointer[10], ~Stack_Pointer[9], ~Stack_Pointer[8], ~Stack_Pointer[7], ~Stack_Pointer[6], ~Stack_Pointer[5], ~Stack_Pointer[4], ~Stack_Pointer[3], ~Stack_Pointer[2], ~Stack_Pointer[1], ~Stack_Pointer[0], Pop);  // AND_Gate
  or or_1 (Error, and_2_out, Sub_Overflow, and_1_out);
endmodule
