// Logisim project traffic_lights_patryk.circ as structural Verilog: 4 circuits, main circuit Traffic Light
module Traffic_Light (
  input  [1:0] Initial,
  input  [4:0] Red,
  input  [4:0] Yellow,
  input  [4:0] Green,
  output Red_2,
  output Yellow_2,
  output Green_2
);

  wire and_1_out, and_2_out, and_3_out, clock_1_out, decoder_1_out0, decoder_1_out1, decoder_1_out2,
       equality_1_eq, equality_2_eq, equality_3_eq, equality_4_eq, or_1_out, or_2_out, or_3_out, or_4_out,
       or_5_out, or_6_out;
  wire [15:0] counter_16b_1_o;

  Clock clock_1 (.out(clock_1_out));
  Counter__16b counter_16b_1 (.C(clock_1_out), .D(16'h1c), .O(counter_16b_1_o));
  Equality equality_1 (.a({5{1'b0}}), .b(counter_16b_1_o[4:0]), .eq(equality_1_eq));
  Equality equality_2 (.a(Red), .b(counter_16b_1_o[4:0]), .eq(equality_2_eq));
  Equality equality_3 (.a(Yellow), .b(counter_16b_1_o[4:0]), .eq(equality_3_eq));
  Equality equality_4 (.a(Green), .b(counter_16b_1_o[4:0]), .eq(equality_4_eq));
  Decoder #(.select(2), .enable("false")) decoder_1 (
    .out0(decoder_1_out0), .out1(decoder_1_out1), .out2(decoder_1_out2), .sel(Initial));  // open: out3
  or or_1 (or_1_out, equality_3_eq, equality_4_eq);
  or or_2 (or_2_out, equality_2_eq, equality_4_eq);
  or or_3 (or_3_out, equality_2_eq, equality_3_eq);
  and and_1 (and_1_out, equality_1_eq, decoder_1_out0);
  and and_2 (and_2_out, equality_1_eq, decoder_1_out1);
  and and_3 (and_3_out, equality_1_eq, decoder_1_out2);
  or or_4 (or_4_out, and_1_out, equality_2_eq);
  or or_5 (or_5_out, and_2_out, equality_3_eq);
  or or_6 (or_6_out, and_3_out, equality_4_eq);
  S_R_Flip_Flop #(.trigger("low")) s_r_ff_1 (
    .S(or_4_out), .clk(clock_1_out), .R(or_1_out), .Q(Red_2));  // open: Qn, preset, reset, en
  S_R_Flip_Flop #(.trigger("low")) s_r_ff_2 (
    .S(or_5_out), .clk(clock_1_out), .R(or_2_out), .Q(Yellow_2));  // open: Qn, preset, reset, en
  S_R_Flip_Flop #(.trigger("low")) s_r_ff_3 (
    .S(or_6_out), .clk(clock_1_out), .R(or_3_out), .Q(Green_2));  // open: Qn, preset, reset, en
endmodule

module Equality (
  input  [4:0] a,
  input  [4:0] b,
  output eq
);

  wire [4:0] xnor_1_out;

  assign xnor_1_out = ~(a ^ b);  // XNOR_Gate xnor_1, 5 bits wide
  and and_1 (eq, xnor_1_out[0], xnor_1_out[1], xnor_1_out[2], xnor_1_out[3], xnor_1_out[4]);
endmodule

module Assignment_Hidden_Component (
);

  wire Light_1_2_green_2, Light_1_2_red_2, Light_1_2_yellow_2, Light_1_green_2, Light_1_red_2,
       Light_1_yellow_2;

  Traffic_Light Light_1 (
    .Red(5'b01100), .Yellow(5'b01000), .Green({5{1'b0}}), .Initial(2'b10), .Red_2(Light_1_red_2),
    .Yellow_2(Light_1_yellow_2), .Green_2(Light_1_green_2));
  LED led_1 (.in(Light_1_red_2));
  LED led_2 (.in(Light_1_yellow_2));
  LED led_3 (.in(Light_1_green_2));
  LED led_4 (.in(Light_1_2_red_2));
  Traffic_Light Light_1_2 (
    .Red(5'b11010), .Yellow(5'b10110), .Green(5'b01110), .Initial(2'b00), .Red_2(Light_1_2_red_2),
    .Yellow_2(Light_1_2_yellow_2), .Green_2(Light_1_2_green_2));
  LED led_5 (.in(Light_1_2_yellow_2));
  LED led_6 (.in(Light_1_2_green_2));
endmodule

module Assignment_Visible_Component (
);

  wire and_1_out, and_2_out, and_3_out, and_4_out, and_5_out, and_6_out, clock_1_out, clock_2_out,
       decoder_1_out0, decoder_1_out1, decoder_1_out2, decoder_2_out0, decoder_2_out1, decoder_2_out2,
       equality_1_eq, equality_2_eq, equality_3_eq, equality_4_eq, equality_5_eq, equality_6_eq,
       equality_7_eq, equality_8_eq, or_1_out, or_2_out, or_3_out, or_4_out, or_5_out, or_6_out, or_7_out,
       or_8_out, or_9_out, or_10_out, or_11_out, or_12_out, s_r_ff_1_q, s_r_ff_2_q, s_r_ff_3_q, s_r_ff_4_q,
       s_r_ff_5_q, s_r_ff_6_q;
  wire [15:0] counter_16b_1_o, counter_16b_2_o;

  Clock clock_1 (.out(clock_1_out));
  Counter__16b counter_16b_1 (.C(clock_1_out), .D(16'h1c), .O(counter_16b_1_o));
  Equality equality_1 (.a({5{1'b0}}), .b(counter_16b_1_o[4:0]), .eq(equality_1_eq));
  Equality equality_2 (.a(5'b01100), .b(counter_16b_1_o[4:0]), .eq(equality_2_eq));
  Equality equality_3 (.a(5'b01000), .b(counter_16b_1_o[4:0]), .eq(equality_3_eq));
  Equality equality_4 (.a({5{1'b0}}), .b(counter_16b_1_o[4:0]), .eq(equality_4_eq));
  or or_1 (or_1_out, equality_3_eq, equality_4_eq);
  or or_2 (or_2_out, equality_2_eq, equality_4_eq);
  or or_3 (or_3_out, equality_2_eq, equality_3_eq);
  Decoder #(.select(2), .enable("false")) decoder_1 (
    .out0(decoder_1_out0), .out1(decoder_1_out1), .out2(decoder_1_out2), .sel(2'b10));  // open: out3
  and and_1 (and_1_out, equality_1_eq, decoder_1_out0);
  or or_4 (or_4_out, and_1_out, equality_2_eq);
  and and_2 (and_2_out, equality_1_eq, decoder_1_out1);
  or or_5 (or_5_out, and_2_out, equality_3_eq);
  and and_3 (and_3_out, equality_1_eq, decoder_1_out2);
  or or_6 (or_6_out, and_3_out, equality_4_eq);
  S_R_Flip_Flop #(.trigger("low")) s_r_ff_1 (
    .S(or_4_out), .clk(clock_1_out), .R(or_1_out), .Q(s_r_ff_1_q));  // open: Qn, preset, reset, en
  S_R_Flip_Flop #(.trigger("low")) s_r_ff_2 (
    .S(or_5_out), .clk(clock_1_out), .R(or_2_out), .Q(s_r_ff_2_q));  // open: Qn, preset, reset, en
  S_R_Flip_Flop #(.trigger("low")) s_r_ff_3 (
    .S(or_6_out), .clk(clock_1_out), .R(or_3_out), .Q(s_r_ff_3_q));  // open: Qn, preset, reset, en
  LED led_1 (.in(s_r_ff_1_q));
  LED led_2 (.in(s_r_ff_2_q));
  LED led_3 (.in(s_r_ff_3_q));
  Clock clock_2 (.out(clock_2_out));
  Counter__16b counter_16b_2 (.C(clock_2_out), .D(16'h1c), .O(counter_16b_2_o));
  Equality equality_5 (.a({5{1'b0}}), .b(counter_16b_2_o[4:0]), .eq(equality_5_eq));
  Equality equality_6 (.a(5'b11010), .b(counter_16b_2_o[4:0]), .eq(equality_6_eq));
  Equality equality_7 (.a(5'b10110), .b(counter_16b_2_o[4:0]), .eq(equality_7_eq));
  Equality equality_8 (.a(5'b01110), .b(counter_16b_2_o[4:0]), .eq(equality_8_eq));
  or or_7 (or_7_out, equality_7_eq, equality_8_eq);
  or or_8 (or_8_out, equality_6_eq, equality_8_eq);
  or or_9 (or_9_out, equality_6_eq, equality_7_eq);
  Decoder #(.select(2), .enable("false")) decoder_2 (
    .out0(decoder_2_out0), .out1(decoder_2_out1), .out2(decoder_2_out2), .sel(2'b00));  // open: out3
  and and_4 (and_4_out, equality_5_eq, decoder_2_out0);
  and and_5 (and_5_out, equality_5_eq, decoder_2_out1);
  and and_6 (and_6_out, equality_5_eq, decoder_2_out2);
  or or_10 (or_10_out, and_4_out, equality_6_eq);
  or or_11 (or_11_out, and_5_out, equality_7_eq);
  or or_12 (or_12_out, and_6_out, equality_8_eq);
  LED led_4 (.in(s_r_ff_4_q));
  S_R_Flip_Flop #(.trigger("low")) s_r_ff_4 (
    .S(or_10_out), .clk(clock_2_out), .R(or_7_out), .Q(s_r_ff_4_q));  // open: Qn, preset, reset, en
  S_R_Flip_Flop #(.trigger("low")) s_r_ff_5 (
    .S(or_11_out), .clk(clock_2_out), .R(or_8_out), .Q(s_r_ff_5_q));  // open: Qn, preset, reset, en
  LED led_5 (.in(s_r_ff_5_q));
  LED led_6 (.in(s_r_ff_6_q));
  S_R_Flip_Flop #(.trigger("low")) s_r_ff_6 (
    .S(or_12_out), .clk(clock_2_out), .R(or_9_out), .Q(s_r_ff_6_q));  // open: Qn, preset, reset, en

  // Notes on the sheet:
  //   Traffic Light 1
  //   Traffic Light 2
endmodule
