// Logisim project SD_Group30.circ as structural Verilog: 8 circuits, main circuit main
module main (
  output [15:0] pc,
  output [15:0] r0,
  output [15:0] r1,
  output [15:0] r2,
  output [15:0] r3,
  output [15:0] r4,
  output [15:0] r5,
  output [15:0] r6,
  output [15:0] r7,
  output halt
);

  wire C, clock_1_out, MemRead, MemWrite, RegWrite, Reset, Shift8;
  wire [1:0] ALUSrc;
  wire [2:0] RegDst, RegSrc, RegT;
  wire [3:0] ALUOp;
  wire [15:0] ALUOut, Instruction, multiplexer_1_out, multiplexer_2_out, ram_2_data, RegDstData, RegSrcData,
       RegTData, Signed_Immediate, Unsigned_Immediate;

  Halt halt_1 (.instruction(Instruction), .clock(clock_1_out), .reset(Reset), .halt(halt));
  Clock clock_1 (.out(clock_1_out));
  Button u_reset (.out(Reset));
  and and_1 (C, ~halt, clock_1_out);  // AND_Gate
  Program_Counter__16b program_counter_16b_1 (
    .branch_value({16{1'b0}}), .branch_relative(1'b0), .branch_absolute(1'b0), .C(C), .reset(Reset),
    .instruction_address(pc));
  RAM #(.addrWidth(16), .dataWidth(16)) ram_1 (
    .addr(pc), .data(Instruction), .clk(C), .ld(1'b1), .clr(Reset));  // open: sel
  Control control_1 (
    .instruction(Instruction), .Shift8(Shift8), .RegDst(RegDst), .RegWrite(RegWrite), .MemRead(MemRead),
    .RegSrc(RegSrc), .MemWrite(MemWrite), .RegT(RegT), .Signed_Immediate(Signed_Immediate),
    .Unsigned_Immediate(Unsigned_Immediate), .ALUSrc(ALUSrc), .ALUOp(ALUOp));
  Register_File__8x16b register_file_8x16b_1 (
    .rd(RegDst), .write(RegWrite), .reset(Reset), .C(C), .Data(RegDstData), .rs(RegSrc), .rt(RegT), .r0(r0),
    .r1(r1), .r2(r2), .r3(r3), .r4(r4), .r5(r5), .r6(r6), .r7(r7), .S(RegSrcData), .T(RegTData));
  _16_bit_ALU u_16_bit_alu_1 (
    .ALU_code(ALUOp), .a(multiplexer_1_out), .b(multiplexer_2_out), .result(ALUOut));  // open: overflow
  Multiplexer #(.width(16), .enable("false")) multiplexer_1 (
    .in0(RegSrcData), .in1({16{1'b0}}), .out(multiplexer_1_out), .sel(Shift8));
  Multiplexer #(.select(2), .width(16), .enable("false")) multiplexer_2 (
    .in0(RegTData), .in1(Signed_Immediate), .in2(Unsigned_Immediate), .in3({16{1'b0}}),
    .out(multiplexer_2_out), .sel(ALUSrc));
  RAM #(.addrWidth(16), .dataWidth(16), .bus("separate")) ram_2 (
    .addr(ALUOut), .din(RegSrcData), .data(ram_2_data), .str(MemWrite), .clk(C), .ld(MemRead), .clr(Reset));  // open: sel
  Multiplexer #(.width(16), .enable("false")) multiplexer_3 (
    .in0(ALUOut), .in1(ram_2_data), .out(RegDstData), .sel(MemRead));

  // Notes on the sheet:
  //   current instruction
  //   clock signal
  //   reset button
  //   DO NOT CHANGE THE INPUTS AND OUTPUTS OF THIS CIRCUIT! Do not add/remove inputs or outputs. Do not even change their location or orientation.
endmodule

module Halt (
  input  [15:0] instruction,
  input  clock,
  input  reset,
  output halt
);

  wire and_1_out, comparator_1_eq, comparator_2_gt, counter_1_carry, or_1_out, or_2_out;
  wire [11:0] counter_1_q;

  Comparator #(.width(16), .mode("unsigned")) comparator_1 (
    .a(instruction), .b({16{1'b0}}), .eq(comparator_1_eq));  // open: gt, lt
  Counter #(.width(12), .max('hfff), .trigger("falling")) counter_1 (
    .Q(counter_1_q), .carry(counter_1_carry), .clk(clock), .clr(reset));  // open: load, D, count
  or or_1 (or_1_out, comparator_1_eq, counter_1_carry);
  Comparator #(.width(12), .mode("unsigned")) comparator_2 (
    .a(counter_1_q), .b({12{1'b0}}), .gt(comparator_2_gt));  // open: eq, lt
  or or_2 (or_2_out, halt, and_1_out);
  and and_1 (and_1_out, or_1_out, comparator_2_gt);
  Register #(.width(1)) register_1 (.D(or_2_out), .Q(halt), .clk(clock), .clr(reset));  // open: en

  // Notes on the sheet:
  //   halt becomes and stays asserted if the instruction is 0000 (not in the first clock cycle) or the end of the counter is reached (2^12)
endmodule

// PC
module Program_Counter__16b (
  input  [15:0] branch_value,
  input  branch_relative,
  input  branch_absolute,
  input  C,
  input  reset,
  output [15:0] instruction_address
);

  wire or_1_out;
  wire [15:0] lcu_adder_16b_1_sum, lcu_adder_16b_2_sum, multiplexer_1_out, multiplexer_2_out;

  LCU_Adder__16b lcu_adder_16b_1 (
    .B(multiplexer_1_out), .A(branch_value), .in_3(branch_relative), .Sum(lcu_adder_16b_1_sum));  // open: Overflow, PG, GG
  Multiplexer #(.width(16), .enable("false")) multiplexer_1 (
    .in0({16{1'b0}}), .in1(instruction_address), .out(multiplexer_1_out), .sel(branch_relative));
  or or_1 (or_1_out, branch_relative, branch_absolute);
  Multiplexer #(.width(16), .enable("false")) multiplexer_2 (
    .in0(lcu_adder_16b_2_sum), .in1(lcu_adder_16b_1_sum), .out(multiplexer_2_out), .sel(or_1_out));
  Register__16b register_16b_1 (.reset(reset), .C(C), .D(multiplexer_2_out), .Q(instruction_address));  // open: write
  LCU_Adder__16b lcu_adder_16b_2 (
    .B({16{1'b0}}), .A(instruction_address), .in_3(1'b1), .Sum(lcu_adder_16b_2_sum));  // open: Overflow, PG, GG
endmodule

module Control (
  input  [15:0] instruction,
  output [2:0] RegDst,
  output RegWrite,
  output MemRead,
  output [2:0] RegSrc,
  output MemWrite,
  output [2:0] RegT,
  output [15:0] Signed_Immediate,
  output [15:0] Unsigned_Immediate,
  output [1:0] ALUSrc,
  output Shift8,
  output [3:0] ALUOp
);

  wire inc_dec;
  wire [3:0] multiplexer_5_out;
  wire [15:0] bit_extender_1_unsigned_output, shift8_1_output, sign_extender_1_sign_extended_output;

  and and_1 (inc_dec, ~instruction[15], ~instruction[14], instruction[13], ~instruction[12], instruction[11], ~instruction[10]);  // AND_Gate
  and and_2 (Shift8, instruction[15], ~instruction[14], ~instruction[13], ~instruction[12], instruction[11]);  // AND_Gate
  Multiplexer #(.select(3), .width(3), .enable("false")) multiplexer_1 (
    .in0(3'b000), .in1(instruction[8:6]), .in2(instruction[8:6]), .in3(instruction[11:9]),
    .in4(instruction[10:8]), .in5(3'b000), .in6(3'b000), .in7(3'b000), .out(RegDst), .sel(instruction[15:13]));
  Multiplexer #(.select(3), .width(3), .enable("false")) multiplexer_2 (
    .in0(3'b000), .in1(instruction[5:3]), .in2(instruction[5:3]), .in3(instruction[8:6]),
    .in4(instruction[10:8]), .in5(3'b000), .in6(3'b000), .in7(3'b000), .out(RegSrc), .sel(instruction[15:13]));
  Multiplexer #(.select(3), .width(3), .enable("false")) multiplexer_3 (
    .in0(3'b000), .in1(3'b000), .in2(instruction[2:0]), .in3(3'b000), .in4(3'b000), .in5(3'b000),
    .in6(3'b000), .in7(3'b000), .out(RegT), .sel(instruction[15:13]));
  Multiplexer #(.select(3), .width(2), .enable("false")) multiplexer_4 (
    .in0(2'b00), .in1({1'b0, inc_dec}), .in2(2'b00), .in3(2'b01), .in4(2'b10), .in5(2'b00), .in6(2'b00),
    .in7(2'b00), .out(ALUSrc), .sel(instruction[15:13]));
  Multiplexer #(.select(2), .width(4), .enable("false")) multiplexer_5 (
    .in0(4'b0011), .in1(4'b0100), .in2(4'b0100), .in3(4'b0101), .out(multiplexer_5_out),
    .sel(instruction[12:11]));
  Multiplexer #(.select(3), .width(4), .enable("false")) multiplexer_6 (
    .in0(4'b0000), .in1(instruction[12:9]), .in2(instruction[12:9]), .in3(4'b0100), .in4(multiplexer_5_out),
    .in5(4'b0000), .in6(4'b0000), .in7(4'b0000), .out(ALUOp), .sel(instruction[15:13]));
  nand nand_1 (RegWrite, instruction[12], instruction[13], instruction[14], ~instruction[15]);  // NAND_Gate
  and and_3 (MemRead, ~instruction[12], instruction[13], instruction[14], ~instruction[15]);  // AND_Gate
  and and_4 (MemWrite, instruction[12], instruction[13], instruction[14], ~instruction[15]);  // AND_Gate
  Bit_Extender bit_extender_1 (.unsigned_input(instruction[7:0]), .unsigned_output(bit_extender_1_unsigned_output));
  Shift8 shift8_1 (.\input (bit_extender_1_unsigned_output), .\output (shift8_1_output));
  Sign_Extender sign_extender_1 (
    .signed_input(instruction[5:0]), .sign_extended_output(sign_extender_1_sign_extended_output));
  Multiplexer #(.width(16), .enable("false")) multiplexer_7 (
    .in0(bit_extender_1_unsigned_output), .in1(shift8_1_output), .out(Unsigned_Immediate), .sel(Shift8));
  Multiplexer #(.width(16), .enable("false")) multiplexer_8 (
    .in0(sign_extender_1_sign_extended_output), .in1({{15{1'b0}}, inc_dec}), .out(Signed_Immediate),
    .sel(inc_dec));

  // Other names for the same wires on the sheet: _0_2[2:0] = instruction[2:0]; _0_5[5:0] = instruction[5:0];
  //   _0_7[7:0] = instruction[7:0]; _3_5[2:0] = instruction[5:3]; _6_8[2:0] = instruction[8:6];
  //   _8_10[2:0] = instruction[10:8]; _9_11[2:0] = instruction[11:9]; _9_12[3:0] = instruction[12:9];
  //   _11_12[1:0] = instruction[12:11]; _12 = instruction[12]; _13_15[2:0] = instruction[15:13]
endmodule

module Sign_Extender (
  input  [5:0] signed_input,
  output [15:0] sign_extended_output
);


  assign sign_extended_output = {{11{signed_input[5]}}, signed_input[4:0]};
endmodule

module Bit_Extender (
  input  [7:0] unsigned_input,
  output [15:0] unsigned_output
);


  assign unsigned_output = {{8{1'b0}}, unsigned_input};
endmodule

// LUI
module Load_Upper_Immediate (
  input  [15:0] Input,
  output [15:0] Output
);
endmodule

module Shift8 (
  input  [15:0] \input ,
  output [15:0] \output 
);


  assign \output  = {\input [7:0], {8{1'b0}}};
endmodule
