// Logisim project overflow_passer_patryk.circ as structural Verilog: 1 circuit, main circuit Overflow Passer
module Overflow_Passer (
  input  [3:0] operation,
  input  add_overflow,
  input  sub_overflow,
  input  inv_overflow,
  input  sla_overflow,
  output Overflow
);

  Multiplexer #(.select(4), .enable("false")) multiplexer_1 (
    .in0(1'b0), .in1(1'b0), .in2(1'b0), .in3(1'b0), .in4(add_overflow), .in5(sub_overflow), .in6(1'b0),
    .in7(1'b0), .in8(1'b0), .in9(1'b0), .in10(inv_overflow), .in11(1'b0), .in12(1'b0), .in13(sla_overflow),
    .in14(1'b0), .in15(1'b0), .out(Overflow), .sel(operation));
endmodule
