// Logisim project shifter_patryk.circ as structural Verilog: 2 circuits, main circuit shift
module shift (
  input  [15:0] A,
  output overflow,
  output [15:0] sll_sla,
  output [15:0] srl,
  output [15:0] sra
);

  overflow_detector overflow_detector_1 (.A_MSB(A[15]), .Result({A[14:0], 1'b0}), .overflow(overflow));

  assign sll_sla = {A[14:0], 1'b0};
  assign sra = {{2{A[15]}}, A[14:1]};
  assign srl = {1'b0, A[15:1]};
endmodule

module overflow_detector (
  input  A_MSB,
  input  [15:0] Result,
  output overflow
);

  xor xor_1 (overflow, A_MSB, Result[15]);
endmodule
