// Logisim project ALU_Group30.circ as structural Verilog: 2 circuits, main circuit main
module main (
  output halt,
  output [8:0] counter,
  output [3:0] op,
  output [15:0] a,
  output [15:0] b,
  output [15:0] oracle,
  output [15:0] result,
  output err_oracle,
  output error,
  output ok,
  output start_delimiter
);

  wire and_1_out, and_2_out, clock_1_out, comparator_1_eq, comparator_2_eq;

  Clock clock_1 (.out(clock_1_out));
  Counter #(.width(9), .max('h1ff), .trigger("falling")) counter_1 (
    .Q(counter), .carry(halt), .clk(clock_1_out));  // open: load, D, count, clr
  RAM #(.addrWidth(12), .dataWidth(4), .bus("separate")) ram_1 (
    .addr({counter, 3'b000}), .data(op), .ld(1'b1));  // open: din, str, sel, clk, clr
  RAM #(.addrWidth(12), .dataWidth(16), .bus("separate")) ram_2 (
    .addr({counter, 3'b001}), .data(a), .ld(1'b1));  // open: din, str, sel, clk, clr
  RAM #(.addrWidth(12), .dataWidth(16), .bus("separate")) ram_3 (
    .addr({counter, 3'b010}), .data(b), .ld(1'b1));  // open: din, str, sel, clk, clr
  RAM #(.addrWidth(12), .dataWidth(16), .bus("separate")) ram_4 (
    .addr({counter, 3'b011}), .data(oracle), .ld(1'b1));  // open: din, str, sel, clk, clr
  RAM #(.addrWidth(12), .dataWidth(1), .bus("separate")) ram_5 (
    .addr({counter, 3'b100}), .data(err_oracle), .ld(1'b1));  // open: din, str, sel, clk, clr
  RAM #(.addrWidth(12), .dataWidth(1), .bus("separate")) ram_6 (
    .addr({counter, 3'b101}), .data(start_delimiter), .ld(1'b1));  // open: din, str, sel, clk, clr
  _16_bit_ALU u_16_bit_alu_1 (.ALU_code(op), .a(a), .b(b), .result(result), .overflow(error));
  Comparator #(.width(1), .mode("unsigned")) comparator_1 (
    .a(error), .b(err_oracle), .eq(comparator_1_eq));  // open: gt, lt
  Comparator #(.width(16)) comparator_2 (.a(result), .b(oracle), .eq(comparator_2_eq));  // open: gt, lt
  and and_1 (and_1_out, comparator_1_eq, error);
  and and_2 (and_2_out, comparator_2_eq, comparator_1_eq, ~error);  // AND_Gate
  or or_1 (ok, and_1_out, and_2_out);

  // Notes on the sheet:
  //   You must complete the circuit '12-bit ALU' instead.
  //   DO NOT EDIT THIS CIRCUIT!
endmodule

module _16_bit_ALU (
  input  [3:0] ALU_code,
  input  [15:0] a,
  input  [15:0] b,
  output [15:0] result,
  output overflow
);

  wire add_1_overflow, inv_overflow, shift_1_overflow, sub_overflow;
  wire [15:0] add_1_sum, and_out, comparator_1_eq, comparator_1_gt, comparator_1_lt, comparator_1_neq,
       inv_sum, not_2_out, not_3_out, not_out, or_out, shift_1_sll_sla, shift_1_sra, shift_1_srl, sub_sum;

  assign not_out = ~a;  // NOT_Gate not, 16 bits wide
  assign and_out = a & b;  // AND_Gate and, 16 bits wide
  assign or_out = a | b;  // OR_Gate or, 16 bits wide
  add add_1 (.Overflow(add_1_overflow), .B(b), .A(a), .in_3(1'b0), .Sum(add_1_sum));  // open: PG, GG
  add sub (.Overflow(sub_overflow), .B(not_2_out), .A(a), .in_3(1'b1), .Sum(sub_sum));  // open: PG, GG
  assign not_2_out = ~b;  // NOT_Gate not_2, 16 bits wide
  comparator comparator_1 (
    .subtraction(sub_sum), .Overflow(sub_overflow), .gt(comparator_1_gt), .lt(comparator_1_lt),
    .eq(comparator_1_eq), .neq(comparator_1_neq));
  add inv (.Overflow(inv_overflow), .B(not_3_out), .A({16{1'b0}}), .in_3(1'b1), .Sum(inv_sum));  // open: PG, GG
  assign not_3_out = ~a;  // NOT_Gate not_3, 16 bits wide
  shift shift_1 (.A(a), .overflow(shift_1_overflow), .sll_sla(shift_1_sll_sla), .srl(shift_1_srl), .sra(shift_1_sra));
  Multiplexer #(.select(4), .width(16), .enable("false")) multiplexer_1 (
    .in0({16{1'b0}}), .in1(not_out), .in2(and_out), .in3(or_out), .in4(add_1_sum), .in5(sub_sum),
    .in6(comparator_1_lt), .in7(comparator_1_gt), .in8(comparator_1_eq), .in9(comparator_1_neq),
    .in10(inv_sum), .in11(shift_1_sll_sla), .in12(shift_1_srl), .in13(shift_1_sll_sla), .in14(shift_1_sra),
    .in15(a), .out(result), .sel(ALU_code));
  Overflow_Passer overflow_passer_1 (
    .add_overflow(add_1_overflow), .sub_overflow(sub_overflow), .inv_overflow(inv_overflow),
    .sla_overflow(shift_1_overflow), .operation(ALU_code), .Overflow(overflow));

  // Notes on the sheet:
  //   This circuit is used as a block in the main circuit, and its layout must remain unchanged. The circuit called "main" should be the main circuit of this file.
  //   Do not change the circuit appearance.
  //   DO NOT CHANGE THE INPUTS AND OUTPUTS OF THIS CIRCUIT!
  //   Do not add/remove inputs or outputs. Do not even change their location or orientation.
endmodule
