// Logisim project SD_Group30.circ as structural Verilog: 6 circuits, main circuit main
module main (
  output [15:0] pc,
  output [15:0] r0,
  output [15:0] r1,
  output [15:0] r2,
  output [15:0] r3,
  output [15:0] r4,
  output [15:0] r5,
  output [15:0] r6,
  output [15:0] r7,
  output halt
);

  wire ALUOverflow, and_2_out, Branch, C, clock_1_out, Exception, Jump, Jump_Register, LUI, MemRead,
       MemWrite, RegWrite, Reset;
  wire [1:0] ALUSrc;
  wire [2:0] RegDst, RegSrc, RegT;
  wire [3:0] ALUOp;
  wire [15:0] ALUOut, Instruction, multiplexer_1_out, multiplexer_2_out, multiplexer_3_out,
       multiplexer_4_out, PC_1, ram_2_data, RegDstData, RegSrcData, RegTData, Signed_Immediate,
       Target_Address, Unsigned_Immediate;

  Halt halt_1 (.instruction(Instruction), .Exception(Exception), .clock(clock_1_out), .reset(Reset), .halt(halt));
  Clock clock_1 (.out(clock_1_out));
  Button u_reset (.out(Reset));
  Multiplexer #(.width(16), .enable("false")) multiplexer_1 (
    .in0(Target_Address), .in1(ALUOut), .out(multiplexer_1_out), .sel(Jump_Register));
  and and_1 (C, ~halt, ~Exception, clock_1_out);  // AND_Gate
  Program_Counter__16b program_counter_16b_1 (
    .branch_value(multiplexer_1_out), .branch_relative(and_2_out), .branch_absolute(Jump), .C(C),
    .reset(Reset), .instruction_address_1(PC_1), .instruction_address(pc));
  and and_2 (and_2_out, ALUOut[0], Branch);
  RAM #(.addrWidth(16), .dataWidth(16)) ram_1 (
    .addr(pc), .data(Instruction), .clk(C), .ld(1'b1), .clr(Reset));  // open: sel
  Exception_Control exception_control_1 (.ALUOverflow(ALUOverflow), .instruction(Instruction), .Exception(Exception));
  Control control_1 (
    .instruction(Instruction), .Jump_Register(Jump_Register), .Jump(Jump), .Branch(Branch),
    .Target_Address(Target_Address), .LUI(LUI), .RegDst(RegDst), .RegWrite(RegWrite), .MemRead(MemRead),
    .RegSrc(RegSrc), .MemWrite(MemWrite), .RegT(RegT), .Signed_Immediate(Signed_Immediate),
    .Unsigned_Immediate(Unsigned_Immediate), .ALUSrc(ALUSrc), .ALUOp(ALUOp));
  Multiplexer #(.width(16), .enable("false")) multiplexer_2 (
    .in0(RegDstData), .in1(PC_1), .out(multiplexer_2_out), .sel(Jump));
  Register_File__8x16b register_file_8x16b_1 (
    .rd(RegDst), .write(RegWrite), .reset(Reset), .C(C), .Data(multiplexer_2_out), .rs(RegSrc), .rt(RegT),
    .r0(r0), .r1(r1), .r2(r2), .r3(r3), .r4(r4), .r5(r5), .r6(r6), .r7(r7), .S(RegSrcData), .T(RegTData));
  Multiplexer #(.width(16), .enable("false")) multiplexer_3 (
    .in0(RegSrcData), .in1({16{1'b0}}), .out(multiplexer_3_out), .sel(LUI));
  Multiplexer #(.select(2), .width(16), .enable("false")) multiplexer_4 (
    .in0(RegTData), .in1(Signed_Immediate), .in2(Unsigned_Immediate), .in3({16{1'b0}}),
    .out(multiplexer_4_out), .sel(ALUSrc));
  _16_bit_ALU u_16_bit_alu_1 (
    .ALU_code(ALUOp), .a(multiplexer_3_out), .b(multiplexer_4_out), .result(ALUOut), .overflow(ALUOverflow));
  RAM #(.addrWidth(16), .dataWidth(16), .bus("separate")) ram_2 (
    .addr(ALUOut), .din(RegTData), .data(ram_2_data), .str(MemWrite), .clk(C), .ld(MemRead), .clr(Reset));  // open: sel
  Multiplexer #(.width(16), .enable("false")) multiplexer_5 (
    .in0(ALUOut), .in1(ram_2_data), .out(RegDstData), .sel(MemRead));

  // Notes on the sheet:
  //   current instruction
  //   clock signal
  //   reset button
  //   DO NOT CHANGE THE INPUTS AND OUTPUTS OF THIS CIRCUIT! Do not add/remove inputs or outputs. Do not even change their location or orientation.
endmodule

module Halt (
  input  [15:0] instruction,
  input  Exception,
  input  clock,
  input  reset,
  output halt
);

  wire and_1_out, comparator_1_eq, comparator_2_gt, counter_1_carry, or_1_out, or_2_out;
  wire [11:0] counter_1_q;

  Comparator #(.width(16), .mode("unsigned")) comparator_1 (
    .a(instruction), .b({16{1'b0}}), .eq(comparator_1_eq));  // open: gt, lt
  Counter #(.width(12), .max('hfff), .trigger("falling")) counter_1 (
    .Q(counter_1_q), .carry(counter_1_carry), .clk(clock), .clr(reset));  // open: load, D, count
  or or_1 (or_1_out, comparator_1_eq, counter_1_carry);
  Comparator #(.width(12), .mode("unsigned")) comparator_2 (
    .a(counter_1_q), .b({12{1'b0}}), .gt(comparator_2_gt));  // open: eq, lt
  or or_2 (or_2_out, halt, Exception, and_1_out);
  and and_1 (and_1_out, or_1_out, comparator_2_gt);
  Register #(.width(1)) register_1 (.D(or_2_out), .Q(halt), .clk(clock), .clr(reset));  // open: en

  // Notes on the sheet:
  //   halt becomes and stays asserted if the instruction is 0000 (not in the first clock cycle) or the end of the counter is reached (2^12)
endmodule

// PC
module Program_Counter__16b (
  input  [15:0] branch_value,
  input  branch_relative,
  input  branch_absolute,
  input  C,
  input  reset,
  output [15:0] instruction_address_1,
  output [15:0] instruction_address
);

  wire or_1_out;
  wire [15:0] lcu_adder_16b_1_sum, multiplexer_1_out, multiplexer_2_out;

  LCU_Adder__16b lcu_adder_16b_1 (
    .B(multiplexer_1_out), .A(branch_value), .in_3(branch_relative), .Sum(lcu_adder_16b_1_sum));  // open: Overflow, PG, GG
  Multiplexer #(.width(16), .enable("false")) multiplexer_1 (
    .in0({16{1'b0}}), .in1(instruction_address), .out(multiplexer_1_out), .sel(branch_relative));
  or or_1 (or_1_out, branch_relative, branch_absolute);
  Multiplexer #(.width(16), .enable("false")) multiplexer_2 (
    .in0(instruction_address_1), .in1(lcu_adder_16b_1_sum), .out(multiplexer_2_out), .sel(or_1_out));
  Register__16b register_16b_1 (.reset(reset), .C(C), .D(multiplexer_2_out), .Q(instruction_address));  // open: write
  LCU_Adder__16b lcu_adder_16b_2 (
    .B({16{1'b0}}), .A(instruction_address), .in_3(1'b1), .Sum(instruction_address_1));  // open: Overflow, PG, GG
endmodule

module Control (
  input  [15:0] instruction,
  output Jump_Register,
  output Jump,
  output Branch,
  output [2:0] RegDst,
  output RegWrite,
  output MemRead,
  output [2:0] RegSrc,
  output MemWrite,
  output [2:0] RegT,
  output [15:0] Signed_Immediate,
  output [15:0] Unsigned_Immediate,
  output [1:0] ALUSrc,
  output LUI,
  output [3:0] ALUOp,
  output [15:0] Target_Address
);

  wire inc_dec, not_1_out;
  wire [3:0] multiplexer_6_out, multiplexer_8_out;
  wire [15:0] bit_extender_1_out, bit_extender_2_out, bit_extender_3_out, bit_extender_4_out,
       multiplexer_11_out, shift8_1_output;

  Multiplexer #(.width(16), .enable("false")) multiplexer_1 (
    .in0(bit_extender_1_out), .in1(Signed_Immediate), .out(Target_Address), .sel(Branch));
  assign bit_extender_1_out = {{4{1'b0}}, instruction[11:0]};  // Bit_Extender bit_extender_1
  and and_1 (inc_dec, ~instruction[15], ~instruction[14], instruction[13], ~instruction[12], instruction[11], ~instruction[10]);  // AND_Gate
  and and_2 (Jump_Register, instruction[15], instruction[14], ~instruction[13]);  // AND_Gate
  and and_3 (Jump, instruction[15], instruction[14]);
  and and_4 (LUI, instruction[15], ~instruction[14], ~instruction[13], ~instruction[12], instruction[11]);  // AND_Gate
  and and_5 (Branch, instruction[15], ~instruction[14], instruction[13]);  // AND_Gate
  Multiplexer #(.select(3), .width(3), .enable("false")) multiplexer_2 (
    .in0(instruction[8:6]), .in1(instruction[8:6]), .in2(instruction[8:6]), .in3(instruction[11:9]),
    .in4(instruction[10:8]), .in5(3'b000), .in6(3'b000), .in7(3'b111), .out(RegDst), .sel(instruction[15:13]));
  Multiplexer #(.select(3), .width(3), .enable("false")) multiplexer_3 (
    .in0(3'b000), .in1(instruction[5:3]), .in2(instruction[5:3]), .in3(instruction[8:6]),
    .in4(instruction[10:8]), .in5(instruction[11:9]), .in6(instruction[10:8]), .in7(3'b000), .out(RegSrc),
    .sel(instruction[15:13]));
  Multiplexer #(.select(3), .width(3), .enable("false")) multiplexer_4 (
    .in0(3'b000), .in1(3'b000), .in2(instruction[2:0]), .in3(instruction[11:9]), .in4(3'b000),
    .in5(instruction[8:6]), .in6(3'b000), .in7(3'b000), .out(RegT), .sel(instruction[15:13]));
  Multiplexer #(.select(3), .width(2), .enable("false")) multiplexer_5 (
    .in0(2'b00), .in1({1'b0, inc_dec}), .in2(2'b00), .in3(2'b01), .in4(2'b10), .in5(2'b00), .in6(2'b01),
    .in7(2'b00), .out(ALUSrc), .sel(instruction[15:13]));
  Multiplexer #(.select(2), .width(4), .enable("false")) multiplexer_6 (
    .in0(4'b0011), .in1(4'b0100), .in2(4'b0100), .in3(4'b0101), .out(multiplexer_6_out),
    .sel(instruction[12:11]));
  Multiplexer #(.select(3), .width(4), .enable("false")) multiplexer_7 (
    .in0(4'b0000), .in1(instruction[12:9]), .in2(instruction[12:9]), .in3(4'b0100), .in4(multiplexer_6_out),
    .in5(multiplexer_8_out), .in6(4'b0100), .in7(4'b0000), .out(ALUOp), .sel(instruction[15:13]));
  Multiplexer #(.width(4), .enable("false")) multiplexer_8 (
    .in0(4'b1000), .in1(4'b0110), .out(multiplexer_8_out), .sel(instruction[12]));
  not not_1 (not_1_out, instruction[12]);
  Multiplexer #(.select(3), .enable("false")) multiplexer_9 (
    .in0(1'b1), .in1(1'b1), .in2(1'b1), .in3(not_1_out), .in4(1'b1), .in5(1'b0), .in6(1'b0),
    .in7(instruction[12]), .out(RegWrite), .sel(instruction[15:13]));
  and and_6 (MemRead, ~instruction[12], instruction[13], instruction[14], ~instruction[15]);  // AND_Gate
  and and_7 (MemWrite, instruction[12], instruction[13], instruction[14], ~instruction[15]);  // AND_Gate
  assign bit_extender_2_out = {{8{1'b0}}, instruction[7:0]};  // Bit_Extender bit_extender_2
  Shift8 shift8_1 (.\input (bit_extender_2_out), .\output (shift8_1_output));
  assign bit_extender_3_out = {{10{instruction[5]}}, instruction[5:0]};  // Bit_Extender bit_extender_3
  assign bit_extender_4_out = {{8{instruction[7]}}, instruction[7:0]};  // Bit_Extender bit_extender_4
  Multiplexer #(.width(16), .enable("false")) multiplexer_10 (
    .in0(bit_extender_2_out), .in1(shift8_1_output), .out(Unsigned_Immediate), .sel(LUI));
  Multiplexer #(.select(3), .width(16), .enable("false")) multiplexer_11 (
    .in0({16{1'b0}}), .in1({16{1'b0}}), .in2({16{1'b0}}), .in3(bit_extender_3_out), .in4({16{1'b0}}),
    .in5(bit_extender_3_out), .in6(bit_extender_4_out), .in7({16{1'b0}}), .out(multiplexer_11_out),
    .sel(instruction[15:13]));
  Multiplexer #(.width(16), .enable("false")) multiplexer_12 (
    .in0(multiplexer_11_out), .in1({{15{1'b0}}, inc_dec}), .out(Signed_Immediate), .sel(inc_dec));

  // Other names for the same wires on the sheet: _0_2[2:0] = instruction[2:0]; _0_5[5:0] = instruction[5:0];
  //   _0_7[7:0] = instruction[7:0]; _0_11[11:0] = instruction[11:0]; _3_5[2:0] = instruction[5:3];
  //   _6_8[2:0] = instruction[8:6]; _8_10[2:0] = instruction[10:8]; _9_11[2:0] = instruction[11:9];
  //   _9_12[3:0] = instruction[12:9]; _11_12[1:0] = instruction[12:11]; _12 = instruction[12];
  //   _13_15[2:0] = instruction[15:13]
endmodule

module Shift8 (
  input  [15:0] \input ,
  output [15:0] \output 
);


  assign \output  = {\input [7:0], {8{1'b0}}};
endmodule

module Exception_Control (
  input  ALUOverflow,
  input  [15:0] instruction,
  output Exception
);

  wire and_1_out, and_2_out, and_3_out, and_5_out, and_6_out, InvalidBinary, InvalidJR, InvalidUnary,
       InvalidZero, multiplexer_1_out, multiplexer_2_out, nor_1_out, or_1_out, or_2_out, or_4_out;

  Multiplexer #(.select(4), .enable("false")) multiplexer_1 (
    .in0(1'b1), .in1(1'b0), .in2(1'b1), .in3(1'b1), .in4(1'b0), .in5(1'b0), .in6(1'b1), .in7(1'b1),
    .in8(1'b1), .in9(1'b1), .in10(1'b0), .in11(1'b0), .in12(1'b0), .in13(1'b0), .in14(1'b0), .in15(1'b0),
    .out(multiplexer_1_out), .sel(instruction[12:9]));
  and and_1 (and_1_out, instruction[13], ~instruction[14], ~instruction[15]);  // AND_Gate
  or or_1 (or_1_out, instruction[0], instruction[1], instruction[2]);
  or or_2 (or_2_out, instruction[9], instruction[10], instruction[11], instruction[12], instruction[0], instruction[1], instruction[2], instruction[3], instruction[4], instruction[5]);
  nor nor_1 (nor_1_out, instruction[13], instruction[14], instruction[15]);
  and and_2 (and_2_out, multiplexer_1_out, and_1_out);
  and and_3 (and_3_out, and_1_out, or_1_out);
  and and_4 (InvalidZero, or_2_out, nor_1_out);
  or or_3 (InvalidUnary, and_2_out, and_3_out);
  Multiplexer #(.select(4), .enable("false")) multiplexer_2 (
    .in0(1'b1), .in1(1'b1), .in2(1'b0), .in3(1'b0), .in4(1'b0), .in5(1'b0), .in6(1'b0), .in7(1'b0),
    .in8(1'b0), .in9(1'b0), .in10(1'b1), .in11(1'b1), .in12(1'b1), .in13(1'b1), .in14(1'b1), .in15(1'b1),
    .out(multiplexer_2_out), .sel(instruction[12:9]));
  and and_5 (and_5_out, ~instruction[13], instruction[14], ~instruction[15]);  // AND_Gate
  or or_4 (or_4_out, instruction[11], instruction[12]);
  and and_6 (and_6_out, ~instruction[13], instruction[14], instruction[15]);  // AND_Gate
  and and_7 (InvalidBinary, multiplexer_2_out, and_5_out);
  and and_8 (InvalidJR, or_4_out, and_6_out);
  or or_5 (Exception, ALUOverflow, InvalidZero, InvalidUnary, InvalidBinary, InvalidJR);

  // Other names for the same wires on the sheet: _0_11[11:0] = instruction[11:0]; _8_10[2:0] = instruction[10:8];
  //   _9_11[2:0] = instruction[11:9]; _9_12[3:0] = instruction[12:9]; _11_12[1:0] = instruction[12:11];
  //   _12 = instruction[12]; _0_2[2:0] = instruction[2:0]; _0_5[5:0] = instruction[5:0]; _0_7[7:0] = instruction[7:0];
  //   _3_5[2:0] = instruction[5:3]; _6_8[2:0] = instruction[8:6]; _13_15[2:0] = instruction[15:13]
endmodule
