// Logisim project adder_patryk.circ as structural Verilog: 7 circuits, main circuit Carry Lookahead Adder (4b) (No Overflow Detector)
// CLA Adder
module Carry_Lookahead_Adder__4b___No_Overflow_Detector (
  input  [3:0] B,
  input  [3:0] A,
  input  Carry_In,
  output [3:0] Sum,
  output PG,
  output GG
);

  wire lookahead_carry_unit_4b_1_c1, lookahead_carry_unit_4b_1_c2, lookahead_carry_unit_4b_1_c3;
  wire [3:0] adder_1b_non_msb_4_g, adder_1b_non_msb_4_p;

  Adder__1b___Non_MSB adder_1b_non_msb_1 (
    .A(A[3]), .B(B[3]), .Carry_In(lookahead_carry_unit_4b_1_c3), .p(adder_1b_non_msb_4_p[3]),
    .g(adder_1b_non_msb_4_g[3]), .Sum(Sum[3]));
  Adder__1b___Non_MSB adder_1b_non_msb_2 (
    .A(A[1]), .B(B[1]), .Carry_In(lookahead_carry_unit_4b_1_c1), .p(adder_1b_non_msb_4_p[1]),
    .g(adder_1b_non_msb_4_g[1]), .Sum(Sum[1]));
  Adder__1b___Non_MSB adder_1b_non_msb_3 (
    .A(A[2]), .B(B[2]), .Carry_In(lookahead_carry_unit_4b_1_c2), .p(adder_1b_non_msb_4_p[2]),
    .g(adder_1b_non_msb_4_g[2]), .Sum(Sum[2]));
  Lookahead_Carry_Unit__4b lookahead_carry_unit_4b_1 (
    .p(adder_1b_non_msb_4_p), .g(adder_1b_non_msb_4_g), .c0(Carry_In), .c1(lookahead_carry_unit_4b_1_c1),
    .c2(lookahead_carry_unit_4b_1_c2), .c3(lookahead_carry_unit_4b_1_c3), .GG(GG), .PG(PG));
  Adder__1b___Non_MSB adder_1b_non_msb_4 (
    .A(A[0]), .B(B[0]), .Carry_In(Carry_In), .p(adder_1b_non_msb_4_p[0]), .g(adder_1b_non_msb_4_g[0]),
    .Sum(Sum[0]));
endmodule

module Overflow_Detector_PLA (
  input  A,
  input  B,
  input  Sum,
  output Overflow
);

  wire and_1_out, and_2_out, not_1_out, not_2_out, not_3_out;

  not not_1 (not_1_out, A);
  not not_2 (not_2_out, B);
  not not_3 (not_3_out, Sum);
  and and_1 (and_1_out, not_1_out, not_2_out, Sum);
  and and_2 (and_2_out, A, B, not_3_out);
  or or_1 (Overflow, and_2_out, and_1_out);
endmodule

// LCU
module Lookahead_Carry_Unit__4b (
  input  [3:0] p,
  input  [3:0] g,
  input  c0,
  output c1,
  output c2,
  output c3,
  output GG,
  output PG
);

  wire p0_c0_out, p1_g0_out, p1_p0_c0_out, p2_g1_out, p2_p1_g0_out, p2_p1_p0_c0_out, p3_g2_out, p3_p2_g1_out,
       p3_p2_p1_g0_out;

  and p3_p2_p1_p0 (PG, p[0], p[1], p[2], p[3]);
  and p0_c0 (p0_c0_out, p[0], c0);
  and p1_g0 (p1_g0_out, p[1], g[0]);
  and p1_p0_c0 (p1_p0_c0_out, p[0], p[1], c0);
  and p2_g1 (p2_g1_out, p[2], g[1]);
  and p2_p1_g0 (p2_p1_g0_out, p[2], p[1], g[0]);
  and p2_p1_p0_c0 (p2_p1_p0_c0_out, p[2], p[1], p[0], c0);
  and p3_g2 (p3_g2_out, p[3], g[2]);
  and p3_p2_g1 (p3_p2_g1_out, p[3], p[2], g[1]);
  and p3_p2_p1_g0 (p3_p2_p1_g0_out, p[3], p[2], p[1], g[0]);
  or g0_p0_c0 (c1, g[0], p0_c0_out);
  or g1_p1_g0_p1_p0_c0 (c2, g[1], p1_g0_out, p1_p0_c0_out);
  or g2_p2_g1_p2_p1_g0_p2_p1_p0_c0 (c3, g[2], p2_g1_out, p2_p1_g0_out, p2_p1_p0_c0_out);
  or g3_p3_g2_p3_p2_g1_p3_p2_p1_g0 (GG, g[3], p3_g2_out, p3_p2_g1_out, p3_p2_p1_g0_out);
endmodule

// Adder
module Adder__1b___Non_MSB (
  input  A,
  input  B,
  input  Carry_In,
  output p,
  output g,
  output Sum
);

  wire not_1_out, not_2_out, not_3_out;

  not not_1 (not_1_out, A);
  not not_2 (not_2_out, B);
  not not_3 (not_3_out, Carry_In);
  xor A_B_C (Sum, A, B, Carry_In);
  or A_B (p, A, B);
  and AB (g, A, B);
endmodule

module add (
  input  [15:0] B,
  input  [15:0] A,
  input  in_3,
  output Overflow,
  output [15:0] Sum,
  output PG,
  output GG
);

  wire lookahead_carry_unit_4b_1_c1, lookahead_carry_unit_4b_1_c2, lookahead_carry_unit_4b_1_c3;
  wire [3:0] carry_lookahead_adder_4b_no_overflow_detector_3_gg,
       carry_lookahead_adder_4b_no_overflow_detector_3_pg;

  Carry_Lookahead_Adder__4b___Overflow_Detector carry_lookahead_adder_4b_overflow_detector_1 (
    .Overflow(Overflow), .PG(carry_lookahead_adder_4b_no_overflow_detector_3_pg[3]),
    .GG(carry_lookahead_adder_4b_no_overflow_detector_3_gg[3]), .B(B[15:12]), .A(A[15:12]),
    .Carry_In(lookahead_carry_unit_4b_1_c3), .Sum(Sum[15:12]));
  Carry_Lookahead_Adder__4b___No_Overflow_Detector carry_lookahead_adder_4b_no_overflow_detector_1 (
    .PG(carry_lookahead_adder_4b_no_overflow_detector_3_pg[2]),
    .GG(carry_lookahead_adder_4b_no_overflow_detector_3_gg[2]), .B(B[11:8]), .A(A[11:8]),
    .Carry_In(lookahead_carry_unit_4b_1_c2), .Sum(Sum[11:8]));
  Carry_Lookahead_Adder__4b___No_Overflow_Detector carry_lookahead_adder_4b_no_overflow_detector_2 (
    .PG(carry_lookahead_adder_4b_no_overflow_detector_3_pg[1]),
    .GG(carry_lookahead_adder_4b_no_overflow_detector_3_gg[1]), .B(B[7:4]), .A(A[7:4]),
    .Carry_In(lookahead_carry_unit_4b_1_c1), .Sum(Sum[7:4]));
  Lookahead_Carry_Unit__4b lookahead_carry_unit_4b_1 (
    .p(carry_lookahead_adder_4b_no_overflow_detector_3_pg),
    .g(carry_lookahead_adder_4b_no_overflow_detector_3_gg), .c0(in_3), .c1(lookahead_carry_unit_4b_1_c1),
    .c2(lookahead_carry_unit_4b_1_c2), .c3(lookahead_carry_unit_4b_1_c3), .GG(GG), .PG(PG));
  Carry_Lookahead_Adder__4b___No_Overflow_Detector carry_lookahead_adder_4b_no_overflow_detector_3 (
    .PG(carry_lookahead_adder_4b_no_overflow_detector_3_pg[0]),
    .GG(carry_lookahead_adder_4b_no_overflow_detector_3_gg[0]), .B(B[3:0]), .A(A[3:0]), .Carry_In(in_3),
    .Sum(Sum[3:0]));
endmodule

// Adder (MSB)
module Adder__1b___MSB (
  input  Carry_In,
  input  B,
  input  A,
  output Overflow,
  output Sum,
  output p,
  output g
);

  Overflow_Detector_PLA overflow_detector_pla_1 (.A(A), .B(B), .Sum(Sum), .Overflow(Overflow));
  Adder__1b___Non_MSB adder_1b_non_msb_1 (.A(A), .B(B), .Carry_In(Carry_In), .p(p), .g(g), .Sum(Sum));
endmodule

// CLA Adder (MSB)
module Carry_Lookahead_Adder__4b___Overflow_Detector (
  input  [3:0] B,
  input  [3:0] A,
  input  Carry_In,
  output Overflow,
  output [3:0] Sum,
  output PG,
  output GG
);

  wire lookahead_carry_unit_4b_1_c1, lookahead_carry_unit_4b_1_c2, lookahead_carry_unit_4b_1_c3;
  wire [3:0] adder_1b_non_msb_3_g, adder_1b_non_msb_3_p;

  Adder__1b___MSB adder_1b_msb_1 (
    .Overflow(Overflow), .Carry_In(lookahead_carry_unit_4b_1_c3), .B(B[3]), .A(A[3]), .Sum(Sum[3]),
    .g(adder_1b_non_msb_3_g[3]), .p(adder_1b_non_msb_3_p[3]));
  Adder__1b___Non_MSB adder_1b_non_msb_1 (
    .A(A[2]), .B(B[2]), .Carry_In(lookahead_carry_unit_4b_1_c2), .p(adder_1b_non_msb_3_p[2]),
    .g(adder_1b_non_msb_3_g[2]), .Sum(Sum[2]));
  Adder__1b___Non_MSB adder_1b_non_msb_2 (
    .A(A[1]), .B(B[1]), .Carry_In(lookahead_carry_unit_4b_1_c1), .p(adder_1b_non_msb_3_p[1]),
    .g(adder_1b_non_msb_3_g[1]), .Sum(Sum[1]));
  Lookahead_Carry_Unit__4b lookahead_carry_unit_4b_1 (
    .p(adder_1b_non_msb_3_p), .g(adder_1b_non_msb_3_g), .c0(Carry_In), .c1(lookahead_carry_unit_4b_1_c1),
    .c2(lookahead_carry_unit_4b_1_c2), .c3(lookahead_carry_unit_4b_1_c3), .GG(GG), .PG(PG));
  Adder__1b___Non_MSB adder_1b_non_msb_3 (
    .A(A[0]), .B(B[0]), .Carry_In(Carry_In), .p(adder_1b_non_msb_3_p[0]), .g(adder_1b_non_msb_3_g[0]),
    .Sum(Sum[0]));
endmodule
