// Logisim project comparator_patryk.circ as structural Verilog: 1 circuit, main circuit comparator
module comparator (
  input  [15:0] subtraction,
  input  Overflow,
  output [15:0] gt,
  output [15:0] lt,
  output [15:0] eq,
  output [15:0] neq
);

  wire and_1_out, not_1_out, or_1_out;

  or or_1 (or_1_out, subtraction[0], subtraction[1], subtraction[2], subtraction[3], subtraction[4], subtraction[5], subtraction[6], subtraction[7], subtraction[8], subtraction[9], subtraction[10], subtraction[11], subtraction[12], subtraction[13], subtraction[14]);
  not not_1 (not_1_out, subtraction[15]);
  and and_1 (and_1_out, or_1_out, not_1_out);
  xor xor_1 (lt[0], subtraction[15], Overflow);
  xor xor_2 (gt[0], and_1_out, Overflow);
  and and_2 (eq[0], ~gt[0], ~lt[0]);  // AND_Gate
  not not_2 (neq[0], eq[0]);

  assign eq[15:1] = {15{1'b0}};
  assign gt[15:1] = {15{1'b0}};
  assign lt[15:1] = {15{1'b0}};
  assign neq[15:1] = {15{1'b0}};
endmodule
